# Fritzing sketch scheme (saved by Fritzing 0.8.7b)

parts:
  U1 = ESP8266 NodeMCU LoLin module
  R2 = Resistor [package="2010 [SMD]"]
  RE1 = KY-040 Rotary encoder [package=THT]
  U2 = ESP8266 NodeMCU LoLin module
  R3 = Rotary Potentiometer (Small) [maximum_resistance=100kΩ package=THT]
  R4 = Resistor [package="2010 [SMD]"]
  R5 = Resistor [package="2010 [SMD]"]

nets:
  N1: U1.D0, RE1.DT
  3V3: U1.3V3, RE1.Vcc
  GND: U1.GND, RE1.GND
  N2: U1.D5, RE1.SW
  N3: U1.D6, RE1.CLK
  N4: R2.Pin_0, U2.3V3, R4.Pin_0, R5.Pin_0
  N5: R2.Pin_1, U2.D5
  N6: U2.D0, R3.leg1, R5.Pin_1
  N7: U2.GND, R3.wiper
  N8: U2.D6, R3.leg2, R4.Pin_1

custom parts:
  ESP8266 NodeMCU LoLin module: ESP8266 based NodeMCU
  KY-040 Rotary encoder: KY-040 Rotary Encoder with switch on breakout borad from AZ Delivery
